// Logisim project problem1.circ as structural Verilog
module main (
  input  a,
  input  b,
  input  c,
  input  d,
  output out1,
  output out2
);

  problem1 problem1_1 (.a(a), .b(b), .c(c), .d(d), .out1(out1), .out2(out2));
endmodule

// VHDL entity problem1, as the project stores it:
library ieee;
use ieee.std_logic_1164.all;

entity problem1 is
    port (
        a, b, c, d : in std_logic;
        out1, out2 : out std_logic
    );
end entity problem1;

architecture bhv of problem1 is
begin
    out1 <= a and b and c and d;
    out2 <= a or b or c or d;
end architecture bhv;
