// Logisim project problem2.circ as structural Verilog
module main (
  input  a,
  input  b,
  input  c,
  input  d,
  input  e,
  input  g,
  input  f,
  input  h,
  input  [2:0] ch,
  output data
);

  problem2 problem2_1 (.a(a), .b(b), .c(c), .d(d), .e(e), .f(f), .g(g), .h(h), .ch(ch), .data(data));
endmodule

// VHDL entity problem2, as the project stores it:
library ieee;
use ieee.std_logic_1164.all;

entity problem2 is
    port(
        a, b, c, d, e, f, g, h : in std_logic;
        ch : in std_logic_vector(2 downto 0);
        data : out std_logic
    );
end entity problem2;

architecture bhv of problem2 is
begin
    process(a, b, c, d, e, f, g, h, ch)
    begin
        case ch is
            when "000" => data <= a;
            when "001" => data <= b;
            when "010" => data <= c;
            when "011" => data <= d;
            when "100" => data <= e;
            when "101" => data <= f;
            when "110" => data <= g;
            when "111" => data <= h;
            when others => data <= '0';
        end case;
    end process;
end architecture bhv;
